// Logisim project 1905108-Counter.circ as structural Verilog: 1 circuit, main circuit main
module main (
  input  CLR,
  output y1,
  output y0,
  output y2
);

  wire CLK_out, n7476_1_p3, n7476_1_p9, n7476_1_p11, n7476_1_p13, n7476_2_p7;

  Clock CLK (.out(CLK_out));
  // _7476 7476_1: pin names not known; wires that end beside it: CLK_out, CLR, n7476_1_p3, 1'b1, CLK_out, CLR, 1'b1, y2, n7476_1_p9, 1'b0, n7476_1_p11, y1, n7476_1_p13, 1'b1
  // _7476 7476_2: pin names not known; wires that end beside it: CLK_out, CLR, y1, 1'b1, y1, y0, n7476_2_p7, 1'b0
  // _7432 7432_1: pin names not known; wires that end beside it: n7476_2_p7, n7476_1_p13, n7476_1_p3, n7476_1_p9, n7476_2_p7, n7476_1_p11, 1'b0, 1'b1

  // Notes on the sheet:
  //   Q: 6-1-7-2-5-3-0
endmodule
