// Logisim project 1905108-Ex7 FF.circ as structural Verilog: 1 circuit, main circuit Master-Slave JK FlipFlop
module Master_Slave_JK_FlipFlop (
  input  Initial_value,
  input  J,
  input  K,
  output Q,
  output Q_prime
);

  wire clk_out, n7400_1_p3, n7400_1_p11, n7400_1_p14, n7410_1_p6, n7410_1_p10, n7410_1_p14, n7410_1_p16;

  Clock clk (.out(clk_out));
  // _7410 7410_1: pin names not known; wires that end beside it: J, clk_out, K, clk_out, Q, n7410_1_p6, 1'b0, 1'b1, Q_prime, n7410_1_p10, clk_out, clk_out, clk_out, n7410_1_p14, Initial_value, n7410_1_p16
  // _7400 7400_1: pin names not known; wires that end beside it: n7410_1_p10, n7410_1_p16, n7400_1_p3, n7410_1_p6, n7400_1_p3, n7410_1_p16, 1'b0, 1'b1, n7400_1_p3, n7410_1_p14, n7400_1_p11, n7410_1_p16, n7410_1_p14, n7400_1_p14
  // _7400 7400_2: pin names not known; wires that end beside it: n7400_1_p11, Q_prime, Q, n7400_1_p14, Q, Q_prime, 1'b0, 1'b1

  // Notes on the sheet:
  //   1.Master-Slave JK Flipflop ( NAND implementation )
endmodule
