// Logisim project 1905108-Ex7 Register.circ as structural Verilog: 1 circuit, main circuit 4 bit universal shift register
module _4_bit_universal_shift_register (
  input  Clear,
  input  S1,
  input  S0,
  input  I3,
  input  I2,
  input  I1,
  input  I0,
  input  Shift_left,
  input  Shift_right,
  output A3,
  output A2,
  output A1,
  output A0
);

  wire Clock_out, n7474_1_p1, n74153_1_p7, n74153_2_p8, n74153_2_p10, n74153_2_p18;

  Clock Clock (.out(Clock_out));
  // _74153 74153_1: pin names not known; wires that end beside it: 1'b0, S1, I3, A2, Shift_right, A3, n74153_1_p7, 1'b1, 1'b0, S0, I2, A1, A3, A2
  // _74153 74153_2: pin names not known; wires that end beside it: 1'b0, 1'b0, S1, I1, A0, A2, A1, n74153_2_p8, 1'b0, n74153_2_p10, 1'b1, 1'b0, S0, I0, Shift_left, A1, A0, n74153_2_p18
  // _7474 7474_1: pin names not known; wires that end beside it: n7474_1_p1, n74153_1_p7, Clock_out, A3, 1'b0, 1'b1, n7474_1_p1, n74153_2_p10, Clock_out, A2
  // _7474 7474_2: pin names not known; wires that end beside it: n7474_1_p1, n74153_2_p8, Clock_out, A1, 1'b0, 1'b1, n7474_1_p1, n74153_2_p18, Clock_out, A0
  // _7404 7404_1: pin names not known; wires that end beside it: Clear, n7474_1_p1, 1'b0, 1'b1

  // Notes on the sheet:
  //   2.4bit universal shift register implementation
endmodule
