// Logisim project 1905108.circ as structural Verilog: 2 circuits, main circuit main
module main (
  input  X3,
  input  X2,
  input  X1,
  input  X0,
  output F_X,
  output F_X__prime
);

  wire AND_2_p3, AND_p3, AND_p6, AND_p10, AND_p11, NOT_p2, NOT_p4, NOT_p6, OR_p6, OR_p10;

  // _7404 NOT: pin names not known; wires that end beside it: X3, NOT_p2, X1, NOT_p4, X0, NOT_p6, 1'b0, 1'b1, F_X, F_X__prime
  // _7408 AND: pin names not known; wires that end beside it: X2, NOT_p6, AND_p3, X1, X0, AND_p6, 1'b0, 1'b1, X3, AND_p10, AND_p11
  // _7432 OR: pin names not known; wires that end beside it: AND_p3, AND_p6, AND_p10, NOT_p2, X2, OR_p6, 1'b0, 1'b1, AND_p11, OR_p10, F_X
  // _7408 AND_2: pin names not known; wires that end beside it: NOT_p4, NOT_p6, AND_2_p3, AND_2_p3, OR_p6, OR_p10, 1'b0, 1'b1

  // Notes on the sheet:
  //   x3(x2x0'+x1x0)+x1'x0'(x3'+x2)
  //   1
  //   2
endmodule

module MAIN2 (
  input  [3:0] A,
  input  [3:0] B,
  output out_3
);

  wire AND_p3, AND_p8, main_1_f_x, main_1_f_x__prime, main_2_f_x, main_2_f_x__prime;

  main main_1 (.X3(A[0]), .X2(A[1]), .X1(A[2]), .X0(A[3]), .F_X(main_1_f_x), .F_X__prime(main_1_f_x__prime));
  main main_2 (.X3(B[0]), .X2(B[1]), .X1(B[2]), .X0(B[3]), .F_X(main_2_f_x), .F_X__prime(main_2_f_x__prime));
  // _7408 AND: pin names not known; wires that end beside it: main_1_f_x__prime, main_2_f_x, AND_p3, 1'b0, 1'b1, main_1_f_x, main_2_f_x__prime, AND_p8
  // _7432 OR: pin names not known; wires that end beside it: AND_p8, AND_p3, out_3, 1'b0, 1'b1

  // Notes on the sheet:
  //   F(A)'F(B)+F(A)F(B)'
  //   2
  //   1
endmodule
