// Logisim project 1905108-Ex6.circ as structural Verilog: 1 circuit, main circuit main
module main (
  input  _1,
  input  w,
  input  x,
  input  y,
  input  z,
  output f
);

  wire and_1_out, and_2_out, and_3_out, n74138_1_p8, n74138_1_p9, n74138_1_p10, n74138_2_p9, n74138_2_p11,
       n74138_2_p12, not_1_out;

  not not_1 (not_1_out, w);
  // _74138 74138_1: pin names not known; wires that end beside it: z, y, x, w, w, _1, 1'b1, n74138_1_p8, n74138_1_p9, n74138_1_p10
  // _74138 74138_2: pin names not known; wires that end beside it: 1'b0, z, y, x, not_1_out, not_1_out, _1, 1'b0, n74138_2_p9, 1'b1, n74138_2_p11, n74138_2_p12
  and and_1 (and_1_out, n74138_1_p8, n74138_1_p9, n74138_1_p10, n74138_2_p9);
  and and_2 (and_2_out, n74138_2_p11, n74138_2_p12);
  and and_3 (and_3_out, and_1_out, and_2_out);
  not not_2 (f, and_3_out);

  // Notes on the sheet:
  //   3. f=SUM(1,2,4,6,8,12)
endmodule
