// Logisim project 1905108-Ex7.circ as structural Verilog: 1 circuit, main circuit main
module main (
  input  A,
  input  B,
  input  C,
  input  D,
  input  _1,
  input  _0,
  output f
);

  wire and_1_out, not_1_out, or_1_out;

  and and_1 (and_1_out, C, D);
  or or_1 (or_1_out, C, D);
  not not_1 (not_1_out, _0);
  // _74153 74153_1: pin names not known; wires that end beside it: _0, A, _1, and_1_out, or_1_out, _0, f, 1'b0, 1'b1, not_1_out, B

  // Notes on the sheet:
  //   6.f=SOP(5,6,7,11,12,13,14,15)
endmodule
